// Logisim project Cormac_Passion_Unit.circ as structural Verilog: 1 circuit, main circuit main
module main (
);

  wire and_1_out, and_2_out, and_3_out, and_4_out, clock_1_out, decoder_1_out0, decoder_1_out1,
       decoder_1_out2, decoder_1_out3, or_1_out, or_2_out;
  wire [7:0] adder_1_out, adder_2_out, multiplexer_1_out, multiplexer_2_out, multiplexer_3_out,
       multiplexer_4_out, multiplexer_5_out, multiplexer_6_out, multiplier_1_out, PC_q, ram_1_dout, X0_q,
       X1_q, X2_q, X3_q;
  wire [15:0] Instructions_data;

  ROM #(.dataWidth(16)) Instructions (.addr(PC_q), .data(Instructions_data));
  Register PC (.D(adder_1_out), .en(1'b1), .clk(clock_1_out), .Q(PC_q));  // open: clr
  Adder adder_1 (.a(PC_q), .b(8'h1), .out(adder_1_out));  // open: cin, cout
  or or_1 (or_1_out, Instructions_data[14], Instructions_data[13]);
  or or_2 (or_2_out, or_1_out, Instructions_data[12]);
  Clock clock_1 (.out(clock_1_out));
  Decoder #(.enable("false"), .select(2)) decoder_1 (
    .out0(decoder_1_out0), .out1(decoder_1_out1), .out2(decoder_1_out2), .out3(decoder_1_out3),
    .sel(Instructions_data[10:9]));
  Multiplexer #(.width(8)) multiplexer_1 (
    .in0(multiplexer_3_out), .in1(ram_1_dout), .out(multiplexer_1_out), .sel(Instructions_data[12]));
  and and_1 (and_1_out, or_2_out, decoder_1_out0);
  and and_2 (and_2_out, or_2_out, decoder_1_out1);
  and and_3 (and_3_out, or_2_out, decoder_1_out2);
  and and_4 (and_4_out, or_2_out, decoder_1_out3);
  Multiplexer #(.width(8)) multiplexer_2 (
    .in0(multiplexer_5_out), .in1({1'b0, Instructions_data[6:0]}), .out(multiplexer_2_out),
    .sel(Instructions_data[15]));
  Adder adder_2 (.a(multiplexer_2_out), .b(multiplexer_4_out), .out(adder_2_out));  // open: cin, cout
  RAM #(.trigger("falling")) ram_1 (
    .addr(multiplexer_3_out), .we(Instructions_data[11]), .oe(Instructions_data[12]), .clk(clock_1_out),
    .din(multiplexer_6_out), .dout(ram_1_dout));
  Register X0 (.D(multiplexer_1_out), .en(and_1_out), .clk(clock_1_out), .Q(X0_q));  // open: clr
  Register X1 (.D(multiplexer_1_out), .en(and_2_out), .clk(clock_1_out), .Q(X1_q));  // open: clr
  Register X2 (.D(multiplexer_1_out), .en(and_3_out), .clk(clock_1_out), .Q(X2_q));  // open: clr
  Register X3 (.D(multiplexer_1_out), .en(and_4_out), .clk(clock_1_out), .Q(X3_q));  // open: clr
  Multiplier #(.mode("twosComplement")) multiplier_1 (
    .a(multiplexer_2_out), .b(multiplexer_4_out), .out(multiplier_1_out));  // open: cin, cout
  Multiplexer #(.width(8)) multiplexer_3 (
    .in0(adder_2_out), .in1(multiplier_1_out), .out(multiplexer_3_out), .sel(Instructions_data[13]));
  Multiplexer #(.select(2), .width(8)) multiplexer_4 (
    .in0(X0_q), .in1(X1_q), .in2(X2_q), .in3(X3_q), .out(multiplexer_4_out), .sel(Instructions_data[8:7]));
  Multiplexer #(.select(2), .width(8)) multiplexer_5 (
    .in0(X0_q), .in1(X1_q), .in2(X2_q), .in3(X3_q), .out(multiplexer_5_out), .sel(Instructions_data[1:0]));
  Multiplexer #(.select(2), .width(8)) multiplexer_6 (
    .in0(X0_q), .in1(X1_q), .in2(X2_q), .in3(X3_q), .out(multiplexer_6_out), .sel(Instructions_data[10:9]));

  // Notes on the sheet:
  //   contents of Instructions (hex, n*v repeats v):
  //   c001 c282 4501 2502 a702 8e81 c00 1401 9680
  //   Instruction Memory
  //   Cormac Taylor
  //   I pledge my honor that I have abided by the Stevens Honor System.
  //   Cormac Passion Unit
  //   ALU
  //   Data Memory
  //   Register File
endmodule
